# Fritzing sketch Fade (saved by Fritzing 0.9.2b)

parts:
  WeMos_D1_R1 = WeMos D1 R2
  LED1 = LED - 5mm [color="Red (633nm)" package="5 mm [THT]"]

nets:
  N1: WeMos_D1_R1.D9, LED1.anode
  N2: WeMos_D1_R1.GND, LED1.cathode

custom parts:
  WeMos D1 R2: The D1 R2 is a mini wifi board based on the ESP-8266EX.
